# Fritzing sketch pong (saved by Fritzing 0.9.2b)
breadboards: 1

parts:
  J1 = ATX24 Pin Power Supply Connector [package=atx24_right_angle]
  Composant1 = Arduino Uno (Rev3)
  S1 = Pushbutton [package="[THT]"]
  S2 = Pushbutton [package="[THT]"]
  R1 = Rotary Potentiometer (Small) [maximum_resistance=100kΩ package=THT]
  R2 = Rotary Potentiometer (Small) [maximum_resistance=100kΩ package=THT]
  RGB_SMD_LED1 = SMD RGB LED (WS2812) [package=5050]
  POWER_ON = Pushbutton [package="[THT]"]

nets:
  GND: J1.GND, Composant1.GND, S1.Pin_1, S1.Pin_2, S2.Pin_1, S2.Pin_2, R1.leg1, R2.leg1, RGB_SMD_LED1.VSS, POWER_ON.Pin_1, POWER_ON.Pin_2
  5V: J1.5V, RGB_SMD_LED1.VCC
  N1: J1.PWR_OK, Composant1.D6_PWM
  N2: J1.5V_STDBY, Composant1.5V, R1.leg2, R2.leg2
  N3: J1.PS_ON, Composant1.D5_PWM
  N4: Composant1.A0, R2.wiper
  N5: Composant1.A1, R1.wiper
  N6: Composant1.D10_PWM/SS, RGB_SMD_LED1.DIn
  N7: Composant1.D2, S2.Pin_3, S2.Pin_4
  N8: Composant1.D3_PWM, S1.Pin_3, S1.Pin_4
  N9: Composant1.D4, POWER_ON.Pin_3, POWER_ON.Pin_4
